# Fritzing sketch SensorToAmbient_breadboard_design (saved by Fritzing 0.9.3b)
breadboards: 1

parts:
  VCC1 = Battery
  R1 = Resistor [tolerance=±5% resistance=100k package=THT]
  R2 = Resistor [tolerance=±5% resistance=100k package=THT]
  IC3 = Wio LTE [package=Board]
  Grove1 = Grove Light Sensor
  Grove2 = Grove Light Sensor
  Grove3 = Grove Light Sensor
  Grove4 = Grove Light Sensor
  IC4 = SN74HC125N 3State Buffer [part_number=SN74HC125N package="DIP (Dual Inline) [THT]"]
  RTC1 = RTC-8564NB Akiduki
  LED1 = BlinkM
  VCC2 = Battery

nets:
  GND: VCC1.-, R2.Pin_1, Grove1.Vin-, Grove2.GND, Grove3.GND, RTC1.VSS, LED1.PWR-, VCC2.-
  VCC: VCC1.+, R1.Pin_0, Grove1.Vin+, Grove2.VCC, Grove3.VCC, RTC1.VDD, LED1.PWR+, VCC2.+
  N1: R1.Pin_1, R2.Pin_0, IC3.A5, IC3.3.3V_A4
  N2: IC3.C7, IC4.1OE
  N3: IC3.C6, IC4.2OE
  N4: IC3.B3, Grove2.SCLK, Grove3.SCLK
  N5: IC3.B4, Grove2.MCLK, Grove3.MCLK
  N6: IC3.A7, Grove2.DIN, Grove3.DIN
  N7: IC3.A6, IC4.1Y, IC4.2Y
  N8: IC3.B8, RTC1.SCL, LED1.I2C_SCL
  N9: IC3.B9, RTC1.SDA, LED1.I2C_SDA
  N10: IC3.B7, Grove4.RX
  N11: IC3.B6, Grove4.TX
  N12: IC3.3.3V_UART, Grove4.3.3V
  N13: IC3.GND_UART, Grove4.GND
  N14: IC3.VCC, Grove1.Vout+
  N15: IC3.GND, Grove1.Vout-
  N16: Grove1.EN, RTC1.N.C.
  N17: Grove2.DOUT, IC4.1A
  N18: Grove3.DOUT, IC4.2A

custom parts:
  Wio LTE: While most of smart phones are using LTE network now, how about giving LTE capability to your IoT project with the latest released Wio LTE board. The Wio LTE is an Arduino and Grove compatible development board with also the ability of accessing LTE network. The LTE network provides a wide bandwidth which allows much faster interaction between user and device. The Arduino and Grove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
  Grove Light Sensor: An analog light sensor
  Grove Light Sensor: An analog light sensor
  Grove Light Sensor: An analog light sensor
  SN74HC125N 3State Buffer: These quadruple bus buffer gates feature independent line drivers with 3-state outputs. Each output is disabled when the associated output-enable (OE) input is high.
  BlinkM: BlinkM is a “Smart LED”: a networkable and programmable full-color RGB LED for hobbyists, industrial designers, prototypers, and experimenters. It is designed to allow the easy addition of dynamic indicators, displays, and lighting to existing or new projects. The BlinkM family of Smart LEDs makes it easy to add dynamic stand-alone lighting no matter what your project. If you’ve used up all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
